# Fritzing sketch Wiring (saved by Fritzing 0.9.3b)
breadboards: 6

parts:
  C1 = Electrolytic Capacitor [capacitance=1µF package="100 mil [THT, electrolytic]"]
  Raspberry_Pi_1 = Raspberry Pi 4 [part_number=RPI-4-b]
  S2 = Momentary Switch [package=ksa_sealed_tac_switch]  # not connected
  S3 = Momentary Switch [package=ksa_sealed_tac_switch]  # not connected
  S4 = Momentary Switch [package=ksa_sealed_tac_switch]  # not connected
  U1 = 74HC595 SMD [package="SO16 [SMD]"]
  U2 = 74HC595 SMD [package="SO16 [SMD]"]
  U3 = 74HC595 SMD [package="SO16 [SMD]"]
  U4 = 74HC595 SMD [package="SO16 [SMD]"]
  U5 = 74HC595 SMD [package="SO16 [SMD]"]
  U6 = 74HC595 SMD [package="SO16 [SMD]"]
  U7 = 74HC595 SMD [package="SO16 [SMD]"]
  U8 = 74HC595 SMD [package="SO16 [SMD]"]
  U9 = 74HC595 SMD [package="SO16 [SMD]"]
  U10 = 74HC595 SMD [package="SO16 [SMD]"]
  U11 = 74HC595 SMD [package="SO16 [SMD]"]
  U12 = 74HC595 SMD [package="SO16 [SMD]"]
  U13 = 74HC595 SMD [package="SO16 [SMD]"]
  U14 = 74HC595 SMD [package="SO16 [SMD]"]
  U15 = 74HC595 SMD [package="SO16 [SMD]"]
  U16 = 74HC595 SMD [package="SO16 [SMD]"]
  U17 = 74HC595 SMD [package="SO16 [SMD]"]
  U18 = 74HC595 SMD [package="SO16 [SMD]"]
  U19 = 74HC595 SMD [package="SO16 [SMD]"]
  U20 = 74HC595 SMD [package="SO16 [SMD]"]
  U21 = 74HC595 SMD [package="SO16 [SMD]"]
  U22 = 74HC595 SMD [package="SO16 [SMD]"]
  U23 = 74HC595 SMD [package="SO16 [SMD]"]
  U24 = 74HC595 SMD [package="SO16 [SMD]"]
  U25 = 74HC595 SMD [package="SO16 [SMD]"]
  U26 = 74HC595 SMD [package="SO16 [SMD]"]
  U27 = 74HC595 SMD [package="SO16 [SMD]"]
  U28 = 74HC595 SMD [package="SO16 [SMD]"]
  U29 = 74HC595 SMD [package="SO16 [SMD]"]
  U30 = 74HC595 SMD [package="SO16 [SMD]"]
  U31 = 74HC595 SMD [package="SO16 [SMD]"]
  U32 = 74HC595 SMD [package="SO16 [SMD]"]
  U33 = 74HC595 SMD [package="SO16 [SMD]"]
  U34 = 74HC595 SMD [package="SO16 [SMD]"]
  U35 = 74HC595 SMD [package="SO16 [SMD]"]
  Part1 = Arduino Mega ADK (Rev3)

nets:
  GND: C1.-, Raspberry_Pi_1.GND, U1.GND, U2.GND, U3.GND, U4.GND, U5.GND, U6.GND, U7.GND, U15.GND, U16.GND, U17.GND, U18.GND, U19.GND, U20.GND, U21.GND, U29.GND, U30.GND, U31.GND, U32.GND, U33.GND, U34.GND, U35.GND, Part1.GND
  N1: C1.+, Raspberry_Pi_1.5V
  GND_2: U8.GND, U9.GND, U10.GND, U11.GND, U12.GND, U13.GND, U14.GND, U22.GND, U23.GND, U24.GND, U25.GND, U26.GND, U27.GND, U28.GND

custom parts:
  Raspberry Pi 4: The RPi4, a faster version of the awesome Raspberry Pi 2 B ARM Board with 40 pin gpio. Ready for special Raspberry Pi B+ and RPi2 Hat (Hardware attached (on) top)
